# Fritzing sketch mirror-test v2 (saved by Fritzing 1.0.2b)
breadboards: 1

parts:
  Part1 = Arduino Nano (Rev3.0)
  S1 = Taiway 100-SP-X-T1 SPDT Miniature Toggle Switch [part_number=100-SP-X-T1-0-0-B1-M2 package=THT]
  R1 = Resistor [tolerance=±5% power=0.25W resistance=1k package=THT]
  R2 = Resistor [tolerance=±5% power=0.25W resistance=1k package=THT]
  Part3 = PowerBoost 500 Charger
  U1 = LIPO-1000mAh [package=lipo-1000]
  S2 = Taiway 100-SP-X-T1 SPDT Miniature Toggle Switch [part_number=100-SP-X-T1-0-0-B1-M2 package=THT]
  NEOPIXEL1 = Neopixel Strip -- White (30/m) [part_number=1376]
  NEOPIXEL2 = Neopixel Strip -- White (30/m) [part_number=1376]
  R3 = Resistor [tolerance=±5% power=0.25W resistance=330 package=THT]
  R4 = Resistor [tolerance=±5% power=0.25W resistance=330 package=THT]
  C1 = Capacitor Polarized [package=cpol-radial-1000uf-63v]
  Part4 = PowerBoost 1000 Basic  # not connected

nets:
  GND: Part1.GND, R1.Pin_1, R2.Pin_1, Part3.GND, U1.-, S2.L1, NEOPIXEL1.GND, NEOPIXEL2.GND, C1.-
  N1: Part1.D4, S1.L1, R2.Pin_0
  N2: Part1.D5, S1.L2, R1.Pin_0
  N3: Part1.D7, R3.Pin_0
  N4: Part1.D8, R4.Pin_0
  +5V: Part1.5V, Part3.5.0V, NEOPIXEL1.+5V, NEOPIXEL2.+5V, C1.+
  N5: Part1.3V3, S1.COM
  N6: Part3.VBAT, U1.+
  N7: Part3.ENABLE, S2.COM
  N8: NEOPIXEL1.Din, R3.Pin_1
  N9: NEOPIXEL2.Din, R4.Pin_1

notes:
  Good / Bad Mode Switch
  On/Off Switch

custom parts:
  PowerBoost 500 Charger: The PowerBoost 500C is a little DC/DC boost converter module that can be powered by any 3.7V LiIon/LiPoly battery, and convert the battery output to 5.2V DC for running your 5V projects. At its heart is a TPS61090 boost converter from TI. This boost converter chip has some really nice extras such as low battery detection, 2A internal switch, synchronous conversion, excellent efficiency, and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
  Neopixel Strip -- White (30/m): These NeoPixel strips have 30 digitally-addressable pixel LEDs per meter and are very affordable and are only 12.5 mm wide, 10 mm if you remove the strip from the casing.
  PowerBoost 1000 Basic: The PowerBoost 1000 is a little DC/DC boost converter module that can run from 1.8V batteries or higher, and convert the battery output to 5.2V DC for running your 5V projects. At its heart is a TPS61030 boost converter from TI. This boost converter chip has some really nice extras such as low battery detection, 4A internal switch, synchronous conversion, excellent efficiency, and 700KHz high-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
