# Fritzing sketch mirror-test (saved by Fritzing 1.0.2b)
breadboards: 1

parts:
  Part1 = Arduino Nano (Rev3.0)
  Part2 = 16 NeoPixel Ring [part_number=1463]
  Q1 = Basic FET N-Channel [package="TO220 [THT]"]
  Q2 = Basic FET N-Channel [package="TO220 [THT]"]
  Q3 = Basic FET N-Channel [package="TO220 [THT]"]
  S1 = Taiway 100-SP-X-T1 SPDT Miniature Toggle Switch [part_number=100-SP-X-T1-0-0-B1-M2 package=THT]
  R1 = Resistor [tolerance=±5% power=0.25W resistance=1k package=THT]
  R2 = Resistor [tolerance=±5% power=0.25W resistance=1k package=THT]
  DOTSTAR1 = DotStar Strip -- White (60/m) [part_number=2240]
  Part3 = PowerBoost 500 Charger
  U1 = LIPO-1000mAh [package=lipo-1000]

nets:
  GND: Part1.GND, Part2.GND, Q1.source, Q2.source, Q3.source, R1.Pin_1, R2.Pin_1, Part3.GND, U1.-
  N1: Part1.D4, S1.L1, R2.Pin_0
  N2: Part1.D5, S1.L2, R1.Pin_0
  N3: Part1.D7, Part2.IN
  N4: Part1.D9, Q1.gate
  N5: Part1.D10, Q2.gate
  N6: Part1.D11/MOSI, Q3.gate
  5V: Part1.5V, Part2.VDD, DOTSTAR1.+5V, Part3.5.0V
  N7: Part1.3V3, S1.COM
  N8: Q1.drain, DOTSTAR1.CO
  N9: Q2.drain, DOTSTAR1.GND
  N10: Q3.drain, DOTSTAR1.DO
  N11: Part3.VBAT, U1.+

notes:
  This isn't really a DotStar strip, but actually a 5V RGB strip

custom parts:
  16 NeoPixel Ring: 16 ultra bright smart LED NeoPixels are arranged in a circle with 1.75" (44.5mm) outer diameter. The rings are 'chainable' - connect the output pin of one to the input pin of another. Use only one microcontroller pin to control as many as you can chain together! Each LED is addressable as the driver chip is inside the LED. Each one has ~18mA constant current drive so the color will be very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
  DotStar Strip -- White (60/m): NeopixelDotStar Strip, White, 60 pixels per meter.
  PowerBoost 500 Charger: The PowerBoost 500C is a little DC/DC boost converter module that can be powered by any 3.7V LiIon/LiPoly battery, and convert the battery output to 5.2V DC for running your 5V projects. At its heart is a TPS61090 boost converter from TI. This boost converter chip has some really nice extras such as low battery detection, 2A internal switch, synchronous conversion, excellent efficiency, and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
